// Logisim project project.circ as structural Verilog: 1 circuit, main circuit main
module main (
  input  [3:0] X,
  input  [3:0] Y,
  input  SI,
  input  [3:0] S3S2S1S0,
  output V,
  output C,
  output Z,
  output [3:0] G,
  output N
);

  wire adder_2_cout;
  wire [3:0] adder_1_out, and_1_out, multiplexer_1_out, multiplexer_2_out, not_1_out, not_2_out, or_1_out,
       xor_1_out;

  assign not_1_out = ~X;  // NOT_Gate not_1, 4 bits wide
  assign not_2_out = ~Y;  // NOT_Gate not_2, 4 bits wide
  assign and_1_out = X & Y;  // AND_Gate and_1, 4 bits wide
  assign xor_1_out = X ^ Y;  // XOR_Gate xor_1, 4 bits wide
  assign or_1_out = X | Y;  // OR_Gate or_1, 4 bits wide
  Multiplexer #(.select(2), .width(4)) multiplexer_1 (
    .in0(4'b0000), .in1(X), .in2(not_2_out), .in3(4'b1111), .out(multiplexer_1_out), .sel(S3S2S1S0[2:1]));  // open: en
  Adder #(.width(4)) adder_1 (.a(X), .b(multiplexer_1_out), .out(adder_1_out), .cin(S3S2S1S0[0]), .cout(C));
  Multiplexer #(.select(3), .width(4)) multiplexer_2 (
    .in0(and_1_out), .in1(xor_1_out), .in2(or_1_out), .in3(not_1_out), .in4(not_2_out), .in5({X[2:0], SI}),
    .in6(Y), .in7({Y[0], Y[3:1]}), .out(multiplexer_2_out), .sel(S3S2S1S0[2:0]));  // open: en
  Adder #(.width(3)) adder_2 (.a(X[2:0]), .b(multiplexer_1_out[2:0]), .cout(adder_2_cout));  // open: out, cin
  Multiplexer #(.width(4)) multiplexer_3 (
    .in0(adder_1_out), .in1(multiplexer_2_out), .out(G), .sel(S3S2S1S0[3]));  // open: en
  xor xor_2 (V, adder_2_cout, C);
  nor nor_1 (Z, G[0], G[1], G[2], G[3]);

  assign N = G[3];

  // Notes on the sheet:
  //   PROJCT
endmodule
